# Fritzing sketch test_panel (saved by Fritzing 1.0.5)
breadboards: 2

parts:
  M2 = DOIT Esp32 DevKit v1 (30 pins long, 11 pins width) [part_number=ESP32S-PIN30]
  U3 = MCP23017 [package=dil28-3]
  M3 = DOIT Esp32 DevKit v1 (30 pins long, 11 pins width) [part_number=ESP32S-PIN30]
  part = Resistor [tolerance=±5% power=0.25W resistance=10k package=THT]
  R1 = Resistor [tolerance=±5% power=0.25W resistance=220 package=THT]
  LED1 = LED - 5mm [color="Red (633nm)" current=0.030A package="5 mm [THT]"]
  S1 = Taiway 100-SP-X-T1 SPDT Miniature Toggle Switch [part_number=100-SP-X-T1-0-0-B1-M1 package=THT]

nets:
  3V3: M2.3V3, U3.VCC
  GND: M2.GND, U3.GND, U3.A0, U3.A1, U3.A2, part.Pin_1, LED1.cathode, S1.L1
  N1: M2.RX2, M3.TX2
  N2: M2.TX2, M3.RX2
  N3: M2.D21, U3.SDA
  N4: M2.D22, U3.SCL
  N5: M2.VIN, S1.L2
  N6: U3.GPA7, R1.Pin_1
  N7: U3.RESET, part.Pin_0
  N8: R1.Pin_0, LED1.anode

custom parts:
  DOIT Esp32 DevKit v1 (30 pins long, 11 pins width): The DOIT Esp32 DevKit v1 is one of the development board created by DOIT to evaluate the ESP-WROOM-32 module. It is based on the ESP32 microcontroller that boasts Wifi, Bluetooth, Ethernet and Low Power support all in a single chip. (vanepp) made breadboard work, adjusted pin numbering and labels and reduced size of schematic and cleaned up pcb. This chip is 30pins long (2 x15) and 11 pins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
  MCP23017: 16 bit I/O chip controlled via I2C
